// Logisim project Project.circ as structural Verilog
module Half_Adder (
  input  in_1,
  input  in_2,
  output out_3,
  output out_4
);

  wire not_1_out, or_1_out;

  or or_1 (or_1_out, in_1, in_2);
  and and_1 (out_4, in_1, in_2);
  and and_2 (out_3, or_1_out, not_1_out);
  not not_1 (not_1_out, out_4);
endmodule

module Full_Adder (
  input  in_1,
  input  in_2,
  input  in_3,
  output out_4,
  output out_5
);

  wire half_adder_1_out_3, half_adder_1_out_4, half_adder_2_out_4;

  Half_Adder half_adder_1 (.in_1(in_1), .in_2(in_2), .out_3(half_adder_1_out_3), .out_4(half_adder_1_out_4));
  Half_Adder half_adder_2 (.in_1(half_adder_1_out_3), .in_2(in_3), .out_3(out_4), .out_4(half_adder_2_out_4));
  or or_1 (out_5, half_adder_2_out_4, half_adder_1_out_4);
endmodule

module ALU (
  input  in_1,
  input  in_2,
  input  ALU_Left,
  input  in_4,
  input  in_5,
  input  in_6,
  input  in_7,
  input  in_8,
  input  in_9,
  input  in_10,
  input  in_11,
  input  ALU_Right,
  input  in_13,
  input  in_14,
  input  in_15,
  input  in_16,
  output out_17,
  output out_18,
  output out_19,
  output out_20,
  output out_21,
  output out_22,
  output out_23,
  output out_24,
  output out_25,
  output out_26,
  output out_27,
  output out_28
);

  wire full_adder_1_out_5, full_adder_2_out_5, full_adder_3_out_5, full_adder_4_out_5, full_adder_5_out_5,
       full_adder_6_out_5, half_adder_1_out_4, not_1_out, not_2_out, not_3_out, not_4_out, not_5_out,
       not_6_out, not_7_out, not_8_out;

  Half_Adder half_adder_1 (.in_1(in_8), .in_2(in_16), .out_3(out_17), .out_4(half_adder_1_out_4));
  Full_Adder full_adder_1 (
    .in_1(half_adder_1_out_4), .in_2(in_15), .in_3(in_7), .out_4(out_18), .out_5(full_adder_1_out_5));
  Full_Adder full_adder_2 (
    .in_1(full_adder_1_out_5), .in_2(in_14), .in_3(in_6), .out_4(out_19), .out_5(full_adder_2_out_5));
  Full_Adder full_adder_3 (
    .in_1(full_adder_2_out_5), .in_2(in_13), .in_3(in_5), .out_4(out_20), .out_5(full_adder_3_out_5));
  Full_Adder full_adder_4 (
    .in_1(full_adder_3_out_5), .in_2(ALU_Right), .in_3(in_4), .out_4(out_21), .out_5(full_adder_4_out_5));
  Full_Adder full_adder_5 (
    .in_1(full_adder_4_out_5), .in_2(in_11), .in_3(ALU_Left), .out_4(out_22), .out_5(full_adder_5_out_5));
  Full_Adder full_adder_6 (
    .in_1(full_adder_5_out_5), .in_2(in_10), .in_3(in_2), .out_4(out_23), .out_5(full_adder_6_out_5));
  Full_Adder full_adder_7 (.in_1(full_adder_6_out_5), .in_2(in_9), .in_3(in_1), .out_4(out_24), .out_5(out_25));
  not not_1 (not_1_out, out_23);
  not not_2 (not_2_out, out_24);
  not not_3 (not_3_out, out_22);
  not not_4 (not_4_out, out_20);
  not not_5 (not_5_out, out_21);
  not not_6 (not_6_out, out_18);
  not not_7 (not_7_out, out_19);
  not not_8 (not_8_out, out_17);
  and and_1 (out_26, not_2_out, not_1_out, not_3_out, not_5_out, not_4_out, not_7_out, not_6_out, not_8_out);

  // Notes on the sheet:
  //   Status
endmodule

module _2_s_Complement (
  input  in_1,
  input  in_2,
  input  in_3,
  input  in_4,
  input  in_5,
  input  in_6,
  input  in_7,
  input  in_8,
  output out_9,
  output out_10,
  output out_11,
  output out_12,
  output out_13,
  output out_14,
  output out_15,
  output out_16
);

  wire half_adder_1_out_4, half_adder_2_out_4, half_adder_3_out_4, half_adder_4_out_4, half_adder_5_out_4,
       half_adder_6_out_4, half_adder_7_out_4, not_1_out, not_2_out, not_3_out, not_4_out, not_5_out,
       not_6_out, not_7_out, not_8_out, not_9_out, or_1_out;

  not not_1 (not_1_out, in_2);
  not not_2 (not_2_out, in_1);
  not not_3 (not_3_out, in_6);
  not not_4 (not_4_out, in_3);
  not not_5 (not_5_out, in_4);
  not not_6 (not_6_out, in_5);
  not not_7 (not_7_out, not_8_out);
  not not_8 (not_8_out, in_8);
  not not_9 (not_9_out, in_7);
  or or_1 (or_1_out, not_7_out, not_8_out);
  Half_Adder half_adder_1 (.in_1(or_1_out), .in_2(not_8_out), .out_3(out_16), .out_4(half_adder_1_out_4));
  Half_Adder half_adder_2 (.in_1(half_adder_1_out_4), .in_2(not_9_out), .out_3(out_15), .out_4(half_adder_2_out_4));
  Half_Adder half_adder_3 (.in_1(half_adder_2_out_4), .in_2(not_3_out), .out_3(out_14), .out_4(half_adder_3_out_4));
  Half_Adder half_adder_4 (.in_1(half_adder_3_out_4), .in_2(not_6_out), .out_3(out_13), .out_4(half_adder_4_out_4));
  Half_Adder half_adder_5 (.in_1(half_adder_4_out_4), .in_2(not_5_out), .out_3(out_12), .out_4(half_adder_5_out_4));
  Half_Adder half_adder_6 (.in_1(half_adder_5_out_4), .in_2(not_4_out), .out_3(out_11), .out_4(half_adder_6_out_4));
  Half_Adder half_adder_7 (.in_1(half_adder_6_out_4), .in_2(not_1_out), .out_3(out_10), .out_4(half_adder_7_out_4));
  Half_Adder half_adder_8 (.in_1(half_adder_7_out_4), .in_2(not_2_out), .out_3(out_9));  // open: out_4
endmodule
